# Fritzing sketch scoreboard (saved by Fritzing 0.8.7b)
circuit board: 4.59581cm x 4.12975cm
stripboards: 1

parts:
  BC548B_1 = PNP-Transistor [package="TO92 [THT]"]
  BC548B_2 = PNP-Transistor [package="TO92 [THT]"]
  Raspberry_Pi_Zero = Raspberry Pi A
  X1 = DB9 Connector [package=db9]

nets:
  N1: BC548B_1.E, BC548B_2.E, Raspberry_Pi_Zero.5V, X1.5
  N2: BC548B_1.B, Raspberry_Pi_Zero.GPIO_14
  N3: BC548B_1.C, X1.2
  N4: BC548B_2.B, Raspberry_Pi_Zero.GPIO_15
  N5: BC548B_2.C, X1.3
  N6: Raspberry_Pi_Zero.GND, X1.6

custom parts:
  DB9 Connector: DB9 Connector Standard DB9 (D-Sub 9) serial connector. Can be used for CAN bus as well as RS485 and RS232. Footprint production proven. Spark Fun Electronics SKU : PRT-00429
